// Logisim project 8_BITS_CPU_BEN_EATER.circ as structural Verilog: 15 circuits, main circuit main
module main (
  input  MANUAL_CLOCK,
  input  ENABLE_MANUAL,
  input  in_3
);

  wire AI, AO, BI, CE, CF, CLK, CLR, CO, cpu_alu_1_alu_data_0, cpu_alu_1_alu_data_1, cpu_alu_1_alu_data_2,
       cpu_alu_1_alu_data_3, cpu_alu_1_alu_data_4, cpu_alu_1_alu_data_5, cpu_alu_1_alu_data_6,
       cpu_alu_1_alu_data_7, cpu_ir_1_ir_data_0, cpu_ir_1_ir_data_1, cpu_ir_1_ir_data_2, cpu_ir_1_ir_data_3,
       cpu_ir_1_ir_data_4, cpu_ir_1_ir_data_5, cpu_ir_1_ir_data_6, cpu_ir_1_ir_data_7, cpu_mar_1_mar_data_0,
       cpu_mar_1_mar_data_1, cpu_mar_1_mar_data_2, cpu_mar_1_mar_data_3, cpu_program_counter_1_pc_data_0,
       cpu_program_counter_1_pc_data_1, cpu_program_counter_1_pc_data_2, cpu_program_counter_1_pc_data_3,
       cpu_register_a_1_r_data_0, cpu_register_a_1_r_data_1, cpu_register_a_1_r_data_2,
       cpu_register_a_1_r_data_3, cpu_register_a_1_r_data_4, cpu_register_a_1_r_data_5,
       cpu_register_a_1_r_data_6, cpu_register_a_1_r_data_7, cpu_register_b_1_r_data_0,
       cpu_register_b_1_r_data_1, cpu_register_b_1_r_data_2, cpu_register_b_1_r_data_3,
       cpu_register_b_1_r_data_4, cpu_register_b_1_r_data_5, cpu_register_b_1_r_data_6,
       cpu_register_b_1_r_data_7, EO, FI, FZ, HLT, II, IO, JUMP, MI, OI, QCKL, RI, RO, SUB;
  wire [3:0] cpu_mar_1_adress_output, INSTRUCTIONS;
  wire [7:0] cpu_output_register_1_hundreds_display, cpu_output_register_1_ones_display,
       cpu_output_register_1_signal_display, cpu_output_register_1_tens_display,
       cpu_register_a_1_register_output, cpu_register_b_1_register_output, ram_1_data;

  CPU_MAR cpu_mar_1 (
    .BUS_INPUT(ram_1_data[3:0]), .CLK(CLK), .CLR(CLR), .MI(MI), .ADRESS_OUTPUT(cpu_mar_1_adress_output),
    .MAR_DATA_3(cpu_mar_1_mar_data_3), .MAR_DATA_0(cpu_mar_1_mar_data_0), .MAR_DATA_1(cpu_mar_1_mar_data_1),
    .MAR_DATA_2(cpu_mar_1_mar_data_2));
  RAM #(.addrWidth(4), .databus("bidir"), .trigger("high")) ram_1 (
    .addr(cpu_mar_1_adress_output), .we(RI), .oe(RO), .data(ram_1_data));
  Button u_CLR (.out(CLR));
  LED led_1 (.in(cpu_mar_1_mar_data_3));
  LED led_2 (.in(cpu_ir_1_ir_data_7));
  LED led_3 (.in(cpu_ir_1_ir_data_6));
  LED led_4 (.in(cpu_ir_1_ir_data_5));
  LED led_5 (.in(cpu_ir_1_ir_data_4));
  CPU_IR cpu_ir_1 (
    .CLK(CLK), .CLR(CLR), .II(II), .IO(IO), .BUS_INPUT(ram_1_data), .CONTENT(ram_1_data),
    .INSTRUCTIONS(INSTRUCTIONS), .IR_DATA_3(cpu_ir_1_ir_data_3), .IR_DATA_4(cpu_ir_1_ir_data_4),
    .IR_DATA_5(cpu_ir_1_ir_data_5), .IR_DATA_0(cpu_ir_1_ir_data_0), .IR_DATA_6(cpu_ir_1_ir_data_6),
    .IR_DATA_7(cpu_ir_1_ir_data_7), .IR_DATA_1(cpu_ir_1_ir_data_1), .IR_DATA_2(cpu_ir_1_ir_data_2));
  LED led_6 (.in(cpu_mar_1_mar_data_2));
  LED led_7 (.in(cpu_mar_1_mar_data_1));
  LED led_8 (.in(cpu_mar_1_mar_data_0));
  LED led_9 (.in(cpu_ir_1_ir_data_3));
  LED led_10 (.in(cpu_ir_1_ir_data_2));
  LED led_11 (.in(cpu_ir_1_ir_data_1));
  LED led_12 (.in(cpu_ir_1_ir_data_0));
  CPU_CONTROL_LOGIC cpu_control_logic_1 (
    .CF(CF), .ZF(FZ), .QCLK(QCKL), .CLR(CLR), .INSTRUCTIONS(INSTRUCTIONS), .CO(CO), .CE(CE), .OI(OI),
    .BI(BI), .SUB(SUB), .EO(EO), .AO(AO), .AI(AI), .II(II), .IO(IO), .RO(RO), .RI(RI), .MI(MI), .HLT(HLT),
    .FI(FI), .JUMP(JUMP));
  CPU_CLK cpu_clk_1 (.ENABLE_MANUAL(ENABLE_MANUAL), .HLT(HLT), .MANUAL_CLOCK(MANUAL_CLOCK), .CLK(CLK), .QCKL(QCKL));
  LED led_13 (.in(ram_1_data[7]));
  LED led_14 (.in(ram_1_data[6]));
  LED led_15 (.in(ram_1_data[5]));
  LED led_16 (.in(ram_1_data[4]));
  LED led_17 (.in(ram_1_data[3]));
  LED led_18 (.in(ram_1_data[2]));
  LED led_19 (.in(ram_1_data[1]));
  LED led_20 (.in(ram_1_data[0]));
  LED led_21 (.in(cpu_register_a_1_r_data_7));
  LED led_22 (.in(cpu_register_a_1_r_data_6));
  LED led_23 (.in(cpu_register_a_1_r_data_5));
  LED led_24 (.in(cpu_register_b_1_r_data_7));
  LED led_25 (.in(cpu_register_b_1_r_data_6));
  LED led_26 (.in(cpu_register_a_1_r_data_4));
  LED led_27 (.in(cpu_register_a_1_r_data_3));
  LED led_28 (.in(cpu_register_a_1_r_data_2));
  LED led_29 (.in(cpu_register_a_1_r_data_1));
  LED led_30 (.in(cpu_register_b_1_r_data_5));
  LED led_31 (.in(cpu_register_b_1_r_data_4));
  LED led_32 (.in(cpu_register_b_1_r_data_3));
  LED led_33 (.in(cpu_register_b_1_r_data_2));
  LED led_34 (.in(cpu_register_a_1_r_data_0));
  CPU_REGISTER_A cpu_register_a_1 (
    .CLK(CLK), .CLR(CLR), .AI(AI), .AO(AO), .BUS_INPUT(ram_1_data),
    .REGISTER_OUTPUT(cpu_register_a_1_register_output), .BUS_OUTPUT(ram_1_data),
    .R_DATA_3(cpu_register_a_1_r_data_3), .R_DATA_4(cpu_register_a_1_r_data_4),
    .R_DATA_5(cpu_register_a_1_r_data_5), .R_DATA_0(cpu_register_a_1_r_data_0),
    .R_DATA_6(cpu_register_a_1_r_data_6), .R_DATA_7(cpu_register_a_1_r_data_7),
    .R_DATA_1(cpu_register_a_1_r_data_1), .R_DATA_2(cpu_register_a_1_r_data_2));
  LED led_35 (.in(cpu_register_b_1_r_data_1));
  LED led_36 (.in(cpu_register_b_1_r_data_0));
  CPU_REGISTER_B cpu_register_b_1 (
    .CLK(CLK), .CLR(CLR), .BI(BI), .BO(1'b0), .BUS_INPUT(ram_1_data),
    .REGISTER_OUTPUT(cpu_register_b_1_register_output), .BUS_OUTPUT(ram_1_data),
    .R_DATA_3(cpu_register_b_1_r_data_3), .R_DATA_4(cpu_register_b_1_r_data_4),
    .R_DATA_5(cpu_register_b_1_r_data_5), .R_DATA_0(cpu_register_b_1_r_data_0),
    .R_DATA_6(cpu_register_b_1_r_data_6), .R_DATA_7(cpu_register_b_1_r_data_7),
    .R_DATA_1(cpu_register_b_1_r_data_1), .R_DATA_2(cpu_register_b_1_r_data_2));
  CPU_OUTPUT_REGISTER cpu_output_register_1 (
    .SIGNED_INT(in_3), .CLR(CLR), .BUS_INPUT(ram_1_data), .OI(OI),
    .TENS_DISPLAY(cpu_output_register_1_tens_display),
    .HUNDREDS_DISPLAY(cpu_output_register_1_hundreds_display),
    .SIGNAL_DISPLAY(cpu_output_register_1_signal_display), .ONES_DISPLAY(cpu_output_register_1_ones_display));
  CPU_PROGRAM_COUNTER cpu_program_counter_1 (
    .JUMP(JUMP), .CE(CE), .CLK(CLK), .CLR(CLR), .CO(CO), .IN_COUNTER(ram_1_data[3:0]),
    .OUT_COUNTER(ram_1_data[3:0]), .PC_DATA_3(cpu_program_counter_1_pc_data_3),
    .PC_DATA_0(cpu_program_counter_1_pc_data_0), .PC_DATA_1(cpu_program_counter_1_pc_data_1),
    .PC_DATA_2(cpu_program_counter_1_pc_data_2));
  CPU_ALU cpu_alu_1 (
    .CLK(CLK), .CLR(CLR), .SUB(SUB), .EO(EO), .FI(FI), .A_INPUT(cpu_register_a_1_register_output),
    .B_INPUT(cpu_register_b_1_register_output), .ALU_OUTPUT(ram_1_data), .CF(CF), .FZ(FZ),
    .ALU_DATA_0(cpu_alu_1_alu_data_0), .ALU_DATA_1(cpu_alu_1_alu_data_1), .ALU_DATA_2(cpu_alu_1_alu_data_2),
    .ALU_DATA_3(cpu_alu_1_alu_data_3), .ALU_DATA_4(cpu_alu_1_alu_data_4), .ALU_DATA_5(cpu_alu_1_alu_data_5),
    .ALU_DATA_6(cpu_alu_1_alu_data_6), .ALU_DATA_7(cpu_alu_1_alu_data_7));
  LED led_37 (.in(cpu_program_counter_1_pc_data_3));
  LED led_38 (.in(cpu_program_counter_1_pc_data_2));
  LED led_39 (.in(cpu_program_counter_1_pc_data_1));
  LED led_40 (.in(cpu_alu_1_alu_data_7));
  LED led_41 (.in(cpu_alu_1_alu_data_6));
  LED led_42 (.in(cpu_alu_1_alu_data_5));
  _7_Segment_Display u_7_segment_display_1 (
    .g(cpu_output_register_1_signal_display[0]), .f(cpu_output_register_1_signal_display[1]),
    .a(cpu_output_register_1_signal_display[6]), .b(cpu_output_register_1_signal_display[5]),
    .e(cpu_output_register_1_signal_display[2]), .d(cpu_output_register_1_signal_display[3]),
    .c(cpu_output_register_1_signal_display[4]));  // open: dp
  LED led_43 (.in(cpu_program_counter_1_pc_data_0));
  LED led_44 (.in(cpu_alu_1_alu_data_4));
  LED led_45 (.in(cpu_alu_1_alu_data_3));
  LED led_46 (.in(cpu_alu_1_alu_data_2));
  LED led_47 (.in(cpu_alu_1_alu_data_1));
  _7_Segment_Display u_7_segment_display_2 (
    .g(cpu_output_register_1_hundreds_display[0]), .f(cpu_output_register_1_hundreds_display[1]),
    .a(cpu_output_register_1_hundreds_display[6]), .b(cpu_output_register_1_hundreds_display[5]),
    .e(cpu_output_register_1_hundreds_display[2]), .d(cpu_output_register_1_hundreds_display[3]),
    .c(cpu_output_register_1_hundreds_display[4]));  // open: dp
  LED led_48 (.in(cpu_alu_1_alu_data_0));
  _7_Segment_Display u_7_segment_display_3 (
    .g(cpu_output_register_1_tens_display[0]), .f(cpu_output_register_1_tens_display[1]),
    .a(cpu_output_register_1_tens_display[6]), .b(cpu_output_register_1_tens_display[5]),
    .e(cpu_output_register_1_tens_display[2]), .d(cpu_output_register_1_tens_display[3]),
    .c(cpu_output_register_1_tens_display[4]));  // open: dp
  _7_Segment_Display u_7_segment_display_4 (
    .g(cpu_output_register_1_ones_display[0]), .f(cpu_output_register_1_ones_display[1]),
    .a(cpu_output_register_1_ones_display[6]), .b(cpu_output_register_1_ones_display[5]),
    .e(cpu_output_register_1_ones_display[2]), .d(cpu_output_register_1_ones_display[3]),
    .c(cpu_output_register_1_ones_display[4]));  // open: dp

  // Notes on the sheet:
  //   CONTROL_LOGIC
  //   INS_REGISTER
  //   CLOCK
  //   MAR
  //   RAM
  //   BUS_CONNECTION
  //   REGISTER_A
  //   REGISTER_B
  //   OUTPUT_REGISTER
  //   PROGRAM_COUNTER
  //   ALU
endmodule

module CPU_CLK (
  input  MANUAL_CLOCK,
  input  ENABLE_MANUAL,
  input  HLT,
  output CLK,
  output QCKL
);

  wire and_1_out, and_2_out, clock_1_out, not_1_out, not_2_out, or_1_out;

  Clock clock_1 (.out(clock_1_out));
  not not_1 (not_1_out, ENABLE_MANUAL);
  and and_1 (and_1_out, clock_1_out, not_1_out);
  or or_1 (or_1_out, and_1_out, and_2_out);
  and and_2 (and_2_out, MANUAL_CLOCK, ENABLE_MANUAL);
  not not_2 (not_2_out, HLT);
  and and_3 (CLK, or_1_out, not_2_out);
  not not_3 (QCKL, CLK);
endmodule

module CPU_REGISTER_A (
  input  [7:0] BUS_INPUT,
  input  CLK,
  input  CLR,
  input  AI,
  input  AO,
  output R_DATA_0,
  output R_DATA_1,
  output R_DATA_2,
  output R_DATA_3,
  output R_DATA_4,
  output R_DATA_5,
  output R_DATA_6,
  output R_DATA_7,
  output [7:0] REGISTER_OUTPUT,
  output [7:0] BUS_OUTPUT
);

  Register register_1 (
    .D(BUS_INPUT), .en(AI), .clk(CLK),
    .Q({R_DATA_7, R_DATA_6, R_DATA_5, R_DATA_4, R_DATA_3, R_DATA_2, R_DATA_1, R_DATA_0}), .clr(CLR));
  assign BUS_OUTPUT = AO ? {R_DATA_7, R_DATA_6, R_DATA_5, R_DATA_4, R_DATA_3, R_DATA_2, R_DATA_1, R_DATA_0} : 8'bz;  // Controlled_Buffer controlled_buffer_1

  assign REGISTER_OUTPUT = {R_DATA_7, R_DATA_6, R_DATA_5, R_DATA_4, R_DATA_3, R_DATA_2, R_DATA_1, R_DATA_0};
endmodule

module CPU_REGISTER_B (
  input  [7:0] BUS_INPUT,
  input  CLK,
  input  CLR,
  input  BI,
  input  BO,
  output R_DATA_0,
  output R_DATA_1,
  output R_DATA_2,
  output R_DATA_3,
  output R_DATA_4,
  output R_DATA_5,
  output R_DATA_6,
  output R_DATA_7,
  output [7:0] REGISTER_OUTPUT,
  output [7:0] BUS_OUTPUT
);

  Register register_1 (
    .D(BUS_INPUT), .en(BI), .clk(CLK),
    .Q({R_DATA_7, R_DATA_6, R_DATA_5, R_DATA_4, R_DATA_3, R_DATA_2, R_DATA_1, R_DATA_0}), .clr(CLR));
  assign BUS_OUTPUT = BO ? {R_DATA_7, R_DATA_6, R_DATA_5, R_DATA_4, R_DATA_3, R_DATA_2, R_DATA_1, R_DATA_0} : 8'bz;  // Controlled_Buffer controlled_buffer_1

  assign REGISTER_OUTPUT = {R_DATA_7, R_DATA_6, R_DATA_5, R_DATA_4, R_DATA_3, R_DATA_2, R_DATA_1, R_DATA_0};
endmodule

module CPU_MAR (
  input  [3:0] BUS_INPUT,
  input  CLK,
  input  CLR,
  input  MI,
  output MAR_DATA_0,
  output MAR_DATA_1,
  output MAR_DATA_2,
  output MAR_DATA_3,
  output [3:0] ADRESS_OUTPUT
);

  Register #(.width(4)) register_1 (.D(BUS_INPUT), .en(MI), .clk(CLK), .Q(ADRESS_OUTPUT), .clr(CLR));

  assign MAR_DATA_0 = ADRESS_OUTPUT[0];
  assign MAR_DATA_1 = ADRESS_OUTPUT[1];
  assign MAR_DATA_2 = ADRESS_OUTPUT[2];
  assign MAR_DATA_3 = ADRESS_OUTPUT[3];
endmodule

module CPU_IR (
  input  [7:0] BUS_INPUT,
  input  CLK,
  input  CLR,
  input  II,
  input  IO,
  output IR_DATA_0,
  output IR_DATA_1,
  output IR_DATA_2,
  output IR_DATA_3,
  output IR_DATA_4,
  output IR_DATA_5,
  output IR_DATA_6,
  output IR_DATA_7,
  output [7:0] CONTENT,
  output [3:0] INSTRUCTIONS
);

  Register register_1 (
    .D(BUS_INPUT), .en(II), .clk(CLK), .Q({INSTRUCTIONS, IR_DATA_3, IR_DATA_2, IR_DATA_1, IR_DATA_0}),
    .clr(CLR));
  assign CONTENT = IO ? {4'b0000, IR_DATA_3, IR_DATA_2, IR_DATA_1, IR_DATA_0} : 8'bz;  // Controlled_Buffer controlled_buffer_1

  assign IR_DATA_4 = INSTRUCTIONS[0];
  assign IR_DATA_5 = INSTRUCTIONS[1];
  assign IR_DATA_6 = INSTRUCTIONS[2];
  assign IR_DATA_7 = INSTRUCTIONS[3];
endmodule

module FULL_ADDER (
  input  CARRY_IN,
  input  A,
  input  B,
  output O,
  output CARRY_OUT
);

  wire and_1_out, and_2_out, and_3_out, and_4_out, and_5_out, and_6_out, and_7_out, not_1_out, not_2_out,
       not_3_out;

  not not_1 (not_1_out, CARRY_IN);
  not not_2 (not_2_out, A);
  not not_3 (not_3_out, B);
  and and_1 (and_1_out, not_1_out, not_2_out, B);
  and and_2 (and_2_out, not_1_out, A, not_3_out);
  and and_3 (and_3_out, CARRY_IN, not_2_out, not_3_out);
  and and_4 (and_4_out, CARRY_IN, A, B);
  and and_5 (and_5_out, A, B);
  and and_6 (and_6_out, CARRY_IN, B);
  and and_7 (and_7_out, CARRY_IN, A);
  or or_1 (O, and_1_out, and_2_out, and_3_out, and_4_out);
  or or_2 (CARRY_OUT, and_5_out, and_6_out, and_7_out);
endmodule

module FULL_ADDER_4BITS (
  input  CARRY_IN,
  input  A0,
  input  A1,
  input  A2,
  input  A3,
  input  B0,
  input  B1,
  input  B2,
  input  B3,
  output [3:0] OSUM,
  output CARRY_OUT
);

  wire CARRY_OUT_0, CARRY_OUT_1, CARRY_OUT_2;

  FULL_ADDER full_adder_1 (.CARRY_IN(CARRY_IN), .A(A0), .B(B0), .O(OSUM[0]), .CARRY_OUT(CARRY_OUT_0));
  FULL_ADDER full_adder_2 (.CARRY_IN(CARRY_OUT_0), .A(A1), .B(B1), .O(OSUM[1]), .CARRY_OUT(CARRY_OUT_1));
  FULL_ADDER full_adder_3 (.CARRY_IN(CARRY_OUT_1), .A(A2), .B(B2), .O(OSUM[2]), .CARRY_OUT(CARRY_OUT_2));
  FULL_ADDER full_adder_4 (.CARRY_IN(CARRY_OUT_2), .A(A3), .B(B3), .O(OSUM[3]), .CARRY_OUT(CARRY_OUT));

  // Other names for the same wires on the sheet: S0 = OSUM[0]; S1 = OSUM[1]; S2 = OSUM[2]; S3 = OSUM[3]
endmodule

module FULL_ADDER_SUBTRACTOR_8BITS (
  input  SUB,
  input  [7:0] A_INPUT,
  input  [7:0] B_INPUT,
  input  EO,
  output [7:0] ALU_DATA,
  output [7:0] ALU_OUTPUT,
  output CF
);

  wire B0, B1, B2, B3, B4, B5, B6, B7, full_adder_4bits_1_carry_out;
  wire [7:0] register_1_q;

  xor xor_1 (B0, B_INPUT[0], SUB);
  xor xor_2 (B1, B_INPUT[1], SUB);
  xor xor_3 (B2, B_INPUT[2], SUB);
  xor xor_4 (B3, B_INPUT[3], SUB);
  xor xor_5 (B4, B_INPUT[4], SUB);
  xor xor_6 (B5, B_INPUT[5], SUB);
  xor xor_7 (B6, B_INPUT[6], SUB);
  xor xor_8 (B7, B_INPUT[7], SUB);
  FULL_ADDER_4BITS full_adder_4bits_1 (
    .CARRY_IN(SUB), .A0(A_INPUT[0]), .A1(A_INPUT[1]), .A2(A_INPUT[2]), .A3(A_INPUT[3]), .B0(B0), .B1(B1),
    .B2(B2), .B3(B3), .OSUM(ALU_DATA[3:0]), .CARRY_OUT(full_adder_4bits_1_carry_out));
  FULL_ADDER_4BITS full_adder_4bits_2 (
    .CARRY_IN(full_adder_4bits_1_carry_out), .A0(A_INPUT[4]), .A1(A_INPUT[5]), .A2(A_INPUT[6]),
    .A3(A_INPUT[7]), .B0(B4), .B1(B5), .B2(B6), .B3(B7), .OSUM(ALU_DATA[7:4]), .CARRY_OUT(CF));
  Register #(.trigger("high")) register_1 (.D(ALU_DATA), .en(1'b1), .clk(1'b1), .Q(register_1_q));  // open: clr
  assign ALU_OUTPUT = EO ? register_1_q : 8'bz;  // Controlled_Buffer controlled_buffer_1

  // Other names for the same wires on the sheet: A0 = A_INPUT[0]; A1 = A_INPUT[1]; A2 = A_INPUT[2]; A3 = A_INPUT[3];
  //   A4 = A_INPUT[4]; A5 = A_INPUT[5]; A6 = A_INPUT[6]; A7 = A_INPUT[7]

  // Notes on the sheet:
  //   FULL_ADDER_SUBTRACTOR_INPUTS
  //   FULL_ADDER_SUBTRACTOR_OUTPUTS
endmodule

module CPU_ALU (
  input  SUB,
  input  [7:0] A_INPUT,
  input  [7:0] B_INPUT,
  input  EO,
  input  FI,
  input  CLK,
  input  CLR,
  output ALU_DATA_0,
  output ALU_DATA_1,
  output ALU_DATA_2,
  output ALU_DATA_3,
  output ALU_DATA_4,
  output ALU_DATA_5,
  output ALU_DATA_6,
  output ALU_DATA_7,
  output [7:0] ALU_OUTPUT,
  output CF,
  output FZ
);

  wire CF_t, FZ_t;

  FULL_ADDER_SUBTRACTOR_8BITS full_adder_subtractor_8bits_1 (
    .SUB(SUB), .A_INPUT(A_INPUT), .B_INPUT(B_INPUT), .EO(EO),
    .ALU_DATA({ALU_DATA_7, ALU_DATA_6, ALU_DATA_5, ALU_DATA_4, ALU_DATA_3, ALU_DATA_2, ALU_DATA_1, ALU_DATA_0}),
    .ALU_OUTPUT(ALU_OUTPUT), .CF(CF_t));
  CPU_FLAGS_ZERO cpu_flags_zero_1 (
    .FZ_INPUT({ALU_DATA_7, ALU_DATA_6, ALU_DATA_5, ALU_DATA_4, ALU_DATA_3, ALU_DATA_2, ALU_DATA_1, ALU_DATA_0}),
    .FZ_OUTPUT(FZ_t));
  CPU_FLAGS_REGISTER cpu_flags_register_1 (
    .CLR(CLR), .FI(FI), .CLK(CLK), .FLAGS_INPUT({FZ_t, CF_t}), .FLAGS_OUTPUT({FZ, CF}));

  // Other names for the same wires on the sheet: CF_OUT = CF; FZ_OUT = FZ;
  //   ALU_DATA[7:0] = {ALU_DATA_7, ALU_DATA_6, ALU_DATA_5, ALU_DATA_4, ALU_DATA_3, ALU_DATA_2, ALU_DATA_1, ALU_DATA_0}

  // Notes on the sheet:
  //   ALU_INPUTS
  //   FULL_ADDER_SUBTRACTOR_8BITS
  //   FLAG_ZERO
  //   FLAGS_REGISTER
  //   ALU_OUTPUTS
endmodule

module CPU_PROGRAM_COUNTER (
  input  [3:0] IN_COUNTER,
  input  CO,
  input  JUMP,
  input  CE,
  input  CLK,
  input  CLR,
  output PC_DATA_0,
  output PC_DATA_1,
  output PC_DATA_2,
  output PC_DATA_3,
  output [3:0] OUT_COUNTER
);

  wire controlled_buffer_1_out, or_1_out;

  or or_1 (or_1_out, JUMP, CE);
  Counter #(.max('hf), .width(4)) counter_1 (
    .clr(CLR), .load(JUMP), .up(1'b1), .clk(controlled_buffer_1_out), .D(IN_COUNTER),
    .Q({PC_DATA_3, PC_DATA_2, PC_DATA_1, PC_DATA_0}));  // open: count, carry
  assign controlled_buffer_1_out = or_1_out ? CLK : 1'bz;  // Controlled_Buffer controlled_buffer_1
  assign OUT_COUNTER = CO ? {PC_DATA_3, PC_DATA_2, PC_DATA_1, PC_DATA_0} : 4'bz;  // Controlled_Buffer controlled_buffer_2
endmodule

module CPU_OUTPUT_REGISTER (
  input  [7:0] BUS_INPUT,
  input  OI,
  input  SIGNED_INT,
  input  CLR,
  output [7:0] ONES_DISPLAY,
  output [7:0] TENS_DISPLAY,
  output [7:0] HUNDREDS_DISPLAY,
  output [7:0] SIGNAL_DISPLAY
);

  wire [7:0] BUS_INPUT_t, register_1_q, rom_1_data, rom_2_data, rom_3_data, rom_4_data;

  assign BUS_INPUT_t = OI ? BUS_INPUT : 8'bz;  // Controlled_Buffer controlled_buffer_1
  Register #(.trigger("high")) register_1 (.D(BUS_INPUT_t), .en(OI), .clk(1'b1), .Q(register_1_q), .clr(CLR));
  ROM #(.addrWidth(9)) rom_1 (.addr({SIGNED_INT, register_1_q}), .data(rom_1_data));
  ROM #(.addrWidth(9)) rom_2 (.addr({SIGNED_INT, register_1_q}), .data(rom_2_data));
  ROM #(.addrWidth(9)) rom_3 (.addr({SIGNED_INT, register_1_q}), .data(rom_3_data));
  ROM #(.addrWidth(9)) rom_4 (.addr({SIGNED_INT, register_1_q}), .data(rom_4_data));
  Register #(.trigger("high")) register_2 (.D(rom_1_data), .en(1'b1), .clk(1'b1), .Q(ONES_DISPLAY), .clr(CLR));
  Register #(.trigger("high")) register_3 (.D(rom_2_data), .en(1'b1), .clk(1'b1), .Q(TENS_DISPLAY), .clr(CLR));
  Register #(.trigger("high")) register_4 (.D(rom_3_data), .en(1'b1), .clk(1'b1), .Q(HUNDREDS_DISPLAY), .clr(CLR));
  Register #(.trigger("high")) register_5 (.D(rom_4_data), .en(1'b1), .clk(1'b1), .Q(SIGNAL_DISPLAY), .clr(CLR));

  // Notes on the sheet:
  //   contents of rom_1 (hex, n*v repeats v):
  //   7e 30 6d 79 33 5b 5f 70 7f 7b 7e 30 6d 79 33 5b 5f 70 7f 7b 7e 30 6d 79 33 5b 5f 70 7f 7b 7e 30 6d
  //   79 33 5b 5f 70 7f 7b 7e 30 6d 79 33 5b 5f 70 7f 7b 7e 30 6d 79 33 5b 5f 70 7f 7b 7e 30 6d 79 33 5b
  //   5f 70 7f 7b 7e 30 6d 79 33 5b 5f 70 7f 7b 7e 30 6d 79 33 5b 5f 70 7f 7b 7e 30 6d 79 33 5b 5f 70 7f
  //   7b 7e 30 6d 79 33 5b 5f 70 7f 7b 7e 30 6d 79 33 5b 5f 70 7f 7b 7e 30 6d 79 33 5b 5f 70 7f 7b 7e 30
  //   6d 79 33 5b 5f 70 7f 7b 7e 30 6d 79 33 5b 5f 70 7f 7b 7e 30 6d 79 33 5b 5f 70 7f 7b 7e 30 6d 79 33
  //   5b 5f 70 7f 7b 7e 30 6d 79 33 5b 5f 70 7f 7b 7e 30 6d 79 33 5b 5f 70 7f 7b 7e 30 6d 79 33 5b 5f 70
  //   7f 7b 7e 30 6d 79 33 5b 5f 70 7f 7b 7e 30 6d 79 33 5b 5f 70 7f 7b 7e 30 6d 79 33 5b 5f 70 7f 7b 7e
  //   30 6d 79 33 5b 5f 70 7f 7b 7e 30 6d 79 33 5b 5f 70 7f 7b 7e 30 6d 79 33 5b 7e 30 6d 79 33 5b 5f 70
  //   7f 7b 7e 30 6d 79 33 5b 5f 70 7f 7b 7e 30 6d 79 33 5b 5f 70 7f 7b 7e 30 6d 79 33 5b 5f 70 7f 7b 7e
  //   30 6d 79 33 5b 5f 70 7f 7b 7e 30 6d 79 33 5b 5f 70 7f 7b 7e 30 6d 79 33 5b 5f 70 7f 7b 7e 30 6d 79
  //   33 5b 5f 70 7f 7b 7e 30 6d 79 33 5b 5f 70 7f 7b 7e 30 6d 79 33 5b 5f 70 7f 7b 7e 30 6d 79 33 5b 5f
  //   70 7f 7b 7e 30 6d 79 33 5b 5f 70 7f 7b 7e 30 6d 79 33 5b 5f 70 7f 70 5f 5b 33 79 6d 30 7e 7b 7f 70
  //   5f 5b 33 79 6d 30 7e 7b 7f 70 5f 5b 33 79 6d 30 7e 7b 7f 70 5f 5b 33 79 6d 30 7e 7b 7f 70 5f 5b 33
  //   79 6d 30 7e 7b 7f 70 5f 5b 33 79 6d 30 7e 7b 7f 70 5f 5b 33 79 6d 30 7e 7b 7f 70 5f 5b 33 79 6d 30
  //   7e 7b 7f 70 5f 5b 33 79 6d 30 7e 7b 7f 70 5f 5b 33 79 6d 30 7e 7b 7f 70 5f 5b 33 79 6d 30 7e 7b 7f
  //   70 5f 5b 33 79 6d 30 7e 7b 7f 70 5f 5b 33 79 6d 30
  //   contents of rom_2 (hex, n*v repeats v):
  //   9*7e 10*30 10*6d 10*79 10*33 10*5b 10*5f 10*70 10*7f 10*7b 10*7e 10*30 10*6d 10*79 10*33 10*5b 10*5f
  //   10*70 10*7f 10*7b 10*7e 10*30 10*6d 10*79 10*33 7*5b 10*7e 10*30 10*6d 10*79 10*33 10*5b 10*5f 10*70
  //   10*7f 10*7b 10*7e 10*30 17*6d 10*30 10*7e 10*7b 10*7f 10*70 10*5f 10*5b 10*33 10*79 10*6d 10*30 9*7e
  //   contents of rom_3 (hex, n*v repeats v):
  //   99*7e 100*30 57*6d 100*7e 57*30 99*7e
  //   contents of rom_4 (hex, n*v repeats v):
  //   384*7e 128*1
endmodule

module CPU_CONTROL_LOGIC (
  input  CF,
  input  ZF,
  input  QCLK,
  input  CLR,
  input  [3:0] INSTRUCTIONS,
  output FI,
  output JUMP,
  output CO,
  output CE,
  output OI,
  output BI,
  output SUB,
  output EO,
  output AO,
  output AI,
  output II,
  output IO,
  output RO,
  output RI,
  output MI,
  output HLT
);

  wire and_1_out, or_1_out, STEP_0, STEP_1, STEP_2;

  and and_1 (and_1_out, STEP_0, STEP_2);
  or or_1 (or_1_out, CLR, and_1_out);
  Counter #(.max('h7), .width(3)) counter_1 (
    .clr(or_1_out), .load(1'b0), .up(1'b1), .clk(QCLK), .Q({STEP_2, STEP_1, STEP_0}));  // open: count, D, carry
  ROM #(.addrWidth(11), .dataWidth(16)) rom_1 (
    .addr({2'b00, ZF, CF, INSTRUCTIONS, STEP_2, STEP_1, STEP_0}),
    .data({HLT, MI, RI, RO, IO, II, AI, AO, EO, SUB, BI, OI, CE, CO, JUMP, FI}));

  // Other names for the same wires on the sheet: INS_1 = INSTRUCTIONS[0]; INS_2 = INSTRUCTIONS[1];
  //   INS_3 = INSTRUCTIONS[2]; INS_4 = INSTRUCTIONS[3]

  // Notes on the sheet:
  //   CONTROL_LOGIC_INPUT
  //   contents of rom_1 (hex, n*v repeats v):
  //   4004 1408 6*0 4004 1408 4800 1200 4*0 4004 1408 4800 1020 281 0 0 0 4004 1408 4800 1020 2c1 0 0 0
  //   4004 1408 4800 2100 4*0 4004 1408 a00 5*0 4004 1408 802 5*0 4004 1408 6*0 4004 1408 6*0 4004 1408
  //   6*0 4004 1408 6*0 4004 1408 6*0 4004 1408 6*0 4004 1408 6*0 4004 1408 110 5*0 4004 1408 8000 5*0
  //   4004 1408 6*0 4004 1408 4800 1200 4*0 4004 1408 4800 1020 281 0 0 0 4004 1408 4800 1020 2c1 0 0 0
  //   4004 1408 4800 2100 4*0 4004 1408 a00 5*0 4004 1408 802 5*0 4004 1408 802 5*0 4004 1408 6*0 4004
  //   1408 6*0 4004 1408 6*0 4004 1408 6*0 4004 1408 6*0 4004 1408 6*0 4004 1408 110 5*0 4004 1408 8000
  //   5*0 4004 1408 6*0 4004 1408 4800 1200 4*0 4004 1408 4800 1020 281 0 0 0 4004 1408 4800 1020 2c1 0 0
  //   0 4004 1408 4800 2100 4*0 4004 1408 a00 5*0 4004 1408 802 5*0 4004 1408 6*0 4004 1408 802 5*0 4004
  //   1408 6*0 4004 1408 6*0 4004 1408 6*0 4004 1408 6*0 4004 1408 6*0 4004 1408 110 5*0 4004 1408 8000
  //   5*0 4004 1408 6*0 4004 1408 4800 1200 4*0 4004 1408 4800 1020 281 0 0 0 4004 1408 4800 1020 2c1 0 0
  //   0 4004 1408 4800 2100 4*0 4004 1408 a00 5*0 4004 1408 802 5*0 4004 1408 802 5*0 4004 1408 802 5*0
  //   4004 1408 6*0 4004 1408 6*0 4004 1408 6*0 4004 1408 6*0 4004 1408 6*0 4004 1408 110 5*0 4004 1408
  //   8000
  //   CONTROL_LOGIC_OUTPUT
endmodule

module CPU_FLAGS_REGISTER (
  input  [1:0] FLAGS_INPUT,
  input  FI,
  input  CLK,
  input  CLR,
  output [1:0] FLAGS_OUTPUT
);

  Register #(.width(2)) register_1 (.D(FLAGS_INPUT), .en(FI), .clk(CLK), .Q(FLAGS_OUTPUT), .clr(CLR));
endmodule

module CPU_FLAGS_ZERO (
  input  [7:0] FZ_INPUT,
  output FZ_OUTPUT
);

  wire and_1_out, and_2_out, nor_1_out, nor_2_out, nor_3_out, nor_4_out;

  nor nor_1 (nor_1_out, FZ_INPUT[0], FZ_INPUT[1]);
  nor nor_2 (nor_2_out, FZ_INPUT[2], FZ_INPUT[3]);
  nor nor_3 (nor_3_out, FZ_INPUT[4], FZ_INPUT[5]);
  nor nor_4 (nor_4_out, FZ_INPUT[6], FZ_INPUT[7]);
  and and_1 (and_1_out, nor_1_out, nor_2_out);
  and and_2 (and_2_out, nor_3_out, nor_4_out);
  and and_3 (FZ_OUTPUT, and_1_out, and_2_out);
endmodule
